# Fritzing sketch 12vRelayBoard (saved by Fritzing 0.7.11b)
breadboards: 1

parts:
  Arduino1 = Arduino
  Q1 = NPN-Transistor [part_number=PN2222A package="TO92 [THT]"]
  R1 = Resistor [tolerance=±5% resistance=10k package=THT]
  R2 = Resistor [tolerance=±5% resistance=1k package=THT]
  LED1 = LED - 3mm [color="Red (633nm)" package="3 mm [THT]"]
  D1 = Rectifier Diode [part_number=1N4001 package="Melf DO-213 AB [SMD]"]

nets:
  N1: Arduino1.GND, Q1.E, R2.Pin_1, LED1.anode, D1.cathode
  N2: Arduino1.+5V, R1.Pin_0
  N3: Q1.B, R1.Pin_1, R2.Pin_0
  N4: Q1.C, LED1.cathode, D1.anode
